# Fritzing sketch led (saved by Fritzing 0.8.7b)
breadboards: 1

parts:
  Εξάρτημα1 = Arduino Uno (Rev3)
  LED1 = smd LED [color="Red (633nm)" package="0603 [SMD]"]

nets:
  N1: Εξάρτημα1.D12/MISO, LED1.anode
  N2: Εξάρτημα1.GND, LED1.cathode
