# Fritzing sketch 2leds (saved by Fritzing 0.9.6b)
breadboards: 1

parts:
  Εξάρτημα1 = Arduino Uno (Rev3)
  LED1 = smd LED [color="Red (633nm)" package="0603 [SMD]"]
  LED2 = LED - 5mm [color="Red (633nm)" current=0.030 package="5 mm [THT]"]

nets:
  N1: Εξάρτημα1.D11_PWM/MOSI, LED2.anode
  N2: Εξάρτημα1.D12/MISO, LED1.anode
  N3: Εξάρτημα1.GND, LED1.cathode, LED2.cathode
