# Fritzing sketch 4leds and 3infrared (saved by Fritzing 0.9.6b)
breadboards: 1

parts:
  Εξάρτημα1 = Arduino Uno (Rev3)
  LED1 = smd LED [color="Red (633nm)" package="0603 [SMD]"]
  LED2 = LED - 5mm [color="Red (633nm)" current=0.030 package="5 mm [THT]"]
  M1 = fc-51 [package=THT]
  LED3 = LED - 5mm [color="Red (633nm)" current=0.030 package="5 mm [THT]"]
  LED4 = LED - 5mm [color="Red (633nm)" current=0.030 package="5 mm [THT]"]
  M2 = fc-51 [package=THT]
  M3 = fc-51 [package=THT]

nets:
  N1: Εξάρτημα1.D9_PWM, LED4.anode
  N2: Εξάρτημα1.D10_PWM/SS, LED3.anode
  N3: Εξάρτημα1.D11_PWM/MOSI, LED2.anode
  N4: Εξάρτημα1.D12/MISO, LED1.anode
  N5: Εξάρτημα1.D5_PWM, M1.pin1
  N6: Εξάρτημα1.D6_PWM, M2.pin1
  N7: Εξάρτημα1.D7, M3.pin1
  N8: Εξάρτημα1.5V, M1.pin3, M2.pin2, M2.pin3, M3.pin3
  N9: Εξάρτημα1.GND, LED1.cathode, LED2.cathode, M1.pin2, LED3.cathode, LED4.cathode, M3.pin2
