# Fritzing sketch LDR (saved by Fritzing 0.9.6b)
breadboards: 1

parts:
  Εξάρτημα1 = Arduino Uno (Rev3)
  LED1 = smd LED [color="Red (633nm)" package="0603 [SMD]"]
  LED2 = LED - 5mm [color="Red (633nm)" current=0.030 package="5 mm [THT]"]
  M1 = fc-51 [package=THT]
  LED3 = LED - 5mm [color="Red (633nm)" current=0.030 package="5 mm [THT]"]
  LED4 = LED - 5mm [color="Red (633nm)" current=0.030 package="5 mm [THT]"]
  M2 = fc-51 [package=THT]
  M3 = fc-51 [package=THT]
  R1 = Resistor [tolerance=±5% power=0.25 resistance=220 package=THT]
  R2 = Resistor [tolerance=±5% power=0.25 resistance=220 package=THT]
  R3 = Resistor [tolerance=±5% power=0.25 resistance=220 package=THT]
  R4 = Resistor [tolerance=±5% power=0.25 resistance=220 package=THT]
  R5 = Photocell (LDR) [package=THT]
  R6 = Resistor [tolerance=±5% power=0.25 resistance=4.7k package=THT]

nets:
  N1: Εξάρτημα1.A0, R5.pin_1, R6.Pin_0
  N2: Εξάρτημα1.D9_PWM, LED4.anode
  N3: Εξάρτημα1.D10_PWM/SS, LED3.anode
  N4: Εξάρτημα1.D11_PWM/MOSI, LED2.anode
  N5: Εξάρτημα1.D12/MISO, LED1.anode
  N6: Εξάρτημα1.GND, M1.pin2, M3.pin2, R1.Pin_0, R2.Pin_0, R3.Pin_0, R4.Pin_0, R6.Pin_1
  N7: Εξάρτημα1.D5_PWM, M1.pin1
  N8: Εξάρτημα1.D6_PWM, M2.pin1
  N9: Εξάρτημα1.D7, M3.pin1
  N10: Εξάρτημα1.5V, M1.pin3, M2.pin2, M2.pin3, M3.pin3, R5.pin_0
  N11: LED1.cathode, R1.Pin_1
  N12: LED2.cathode, R2.Pin_1
  N13: LED3.cathode, R3.Pin_1
  N14: LED4.cathode, R4.Pin_1
