# Fritzing sketch LDR and 4 SENSORS (saved by Fritzing 0.9.6b)
breadboards: 1

parts:
  Εξάρτημα1 = Arduino Uno (Rev3)
  LED1 = smd LED [color="Red (633nm)" package="0603 [SMD]"]
  LED2 = LED - 5mm [color="Red (633nm)" current=0.030 package="5 mm [THT]"]
  M1 = fc-51 [package=THT]
  LED3 = LED - 5mm [color="Red (633nm)" current=0.030 package="5 mm [THT]"]
  LED4 = LED - 5mm [color="Red (633nm)" current=0.030 package="5 mm [THT]"]
  M2 = fc-51 [package=THT]
  M3 = fc-51 [package=THT]
  R1 = Resistor [tolerance=±5% power=0.25 resistance=220 package=THT]
  R2 = Resistor [tolerance=±5% power=0.25 resistance=220 package=THT]
  R3 = Resistor [tolerance=±5% power=0.25 resistance=220 package=THT]
  R4 = Resistor [tolerance=±5% power=0.25 resistance=220 package=THT]
  R5 = Photocell (LDR) [package=THT]
  R6 = Resistor [tolerance=±5% power=0.25 resistance=4.7k package=THT]
  M4 = fc-51 [package=THT]

nets:
  N1: Εξάρτημα1.A0, R5.pin_1, R6.Pin_0
  N2: Εξάρτημα1.D12/MISO, R2.Pin_1
  N3: Εξάρτημα1.D13/SCK, R1.Pin_1
  N4: Εξάρτημα1.D2, R4.Pin_1
  N5: Εξάρτημα1.D3_PWM, R3.Pin_1
  N6: Εξάρτημα1.D4, M4.pin1
  N7: Εξάρτημα1.D5_PWM, M1.pin1
  N8: Εξάρτημα1.D6_PWM, M2.pin1
  N9: Εξάρτημα1.D7, M3.pin1
  N10: Εξάρτημα1.5V, M1.pin3, M2.pin3, M3.pin3, R5.pin_0, M4.pin3
  N11: Εξάρτημα1.GND, LED1.cathode, LED2.cathode, M1.pin2, LED3.cathode, LED4.cathode, M2.pin2, M3.pin2, R6.Pin_1, M4.pin2
  N12: LED1.anode, R1.Pin_0
  N13: LED2.anode, R2.Pin_0
  N14: LED3.anode, R3.Pin_0
  N15: LED4.anode, R4.Pin_0
